// Logisim project summative.circ as structural Verilog: 1 circuit, main circuit main
module main (
  input  A,
  input  B,
  input  C,
  input  D,
  input  _5_EB
);

  wire _5_EB_2_out, _5_EB_3_out, _5_EB_4_out, _5_EB_5_out, _5_EB_6_out, _5_EB_7_out, _5_EB_8_out,
       _5_EB_9_out, _5_EB_10_out, _5_EB_11_out, _5_EB_12_out, _5_EB_out, and_1_out, and_2_out, and_3_out,
       and_4_out, and_5_out, and_6_out, and_7_out, and_8_out, and_9_out, and_10_out, and_11_out, and_12_out,
       and_13_out, and_14_out, and_15_out, and_16_out, and_17_out, and_18_out, not_1_out, not_2_out,
       not_3_out, not_4_out, not_5_out, S1__a_out, S1__c_out, S1__d_out, S1__e_out, S1__f_out, S2__a_out,
       S2__b_out, S2__c_out, S2__d_out, S2__e_out, S2__f_out, S2__g_out;

  not not_1 (not_1_out, A);
  not not_2 (not_2_out, B);
  not not_3 (not_3_out, C);
  not not_4 (not_4_out, D);
  not not_5 (not_5_out, _5_EB);
  and S1__a (S1__a_out, A, B);
  and S1__c (S1__c_out, not_1_out, not_3_out, not_2_out);
  and S1__d (S1__d_out, B, A);
  or S1__e (S1__e_out, A, C, B);
  or S1__f (S1__f_out, not_1_out, not_2_out);
  and and_1 (and_1_out, not_1_out, not_2_out, C, D);
  and and_2 (and_2_out, not_1_out, B, C, not_4_out);
  and and_3 (and_3_out, A, B, not_3_out, D);
  and and_4 (and_4_out, not_1_out, B, C, D);
  and and_5 (and_5_out, A, not_2_out, not_3_out, not_4_out);
  and and_6 (and_6_out, not_1_out, B, not_3_out, not_4_out);
  and and_7 (and_7_out, A, B, C, not_4_out);
  and and_8 (and_8_out, not_1_out, not_2_out, C, D);
  and and_9 (and_9_out, not_1_out, B, C, not_4_out);
  and and_10 (and_10_out, A, not_3_out, D);
  and and_11 (and_11_out, not_1_out, B, C);
  and and_12 (and_12_out, not_1_out, not_2_out, C, D);
  and and_13 (and_13_out, not_1_out, B, not_3_out);
  and and_14 (and_14_out, A, not_3_out, D);
  and and_15 (and_15_out, A, B, C);
  and and_16 (and_16_out, not_1_out, not_2_out, C);
  and and_17 (and_17_out, A, B, not_3_out);
  and and_18 (and_18_out, A, not_3_out, D);
  or u__5_EB (_5_EB_out, S1__a_out, not_5_out);
  or _5_EB_2 (_5_EB_2_out, not_5_out, S1__c_out);
  or _5_EB_3 (_5_EB_3_out, not_5_out, S1__d_out);
  or _5_EB_4 (_5_EB_4_out, not_5_out, S1__e_out);
  or _5_EB_5 (_5_EB_5_out, S1__f_out, not_5_out);
  or S2__a (S2__a_out, and_1_out, and_2_out, and_3_out);
  or S2__b (S2__b_out, and_4_out, and_5_out);
  or S2__c (S2__c_out, and_6_out, and_7_out);
  or S2__d (S2__d_out, and_8_out, and_9_out, and_10_out);
  or S2__e (S2__e_out, D, and_11_out);
  or S2__f (S2__f_out, and_12_out, and_13_out, and_14_out, and_15_out);
  or S2__g (S2__g_out, and_16_out, and_17_out, and_18_out);
  or _5_EB_6 (_5_EB_6_out, not_5_out, S2__a_out);
  or _5_EB_7 (_5_EB_7_out, not_5_out, S2__b_out);
  or _5_EB_8 (_5_EB_8_out, not_5_out, S2__c_out);
  or _5_EB_9 (_5_EB_9_out, not_5_out, S2__d_out);
  or _5_EB_10 (_5_EB_10_out, not_5_out, S2__e_out);
  or _5_EB_11 (_5_EB_11_out, not_5_out, S2__f_out);
  or _5_EB_12 (_5_EB_12_out, not_5_out, S2__g_out);
  _7_Segment_Display #(.active("false")) u_7_segment_display_1 (
    .g(not_5_out), .f(_5_EB_5_out), .a(_5_EB_out), .b(not_5_out), .e(_5_EB_4_out), .d(_5_EB_3_out),
    .c(_5_EB_2_out), .dp(not_5_out));
  _7_Segment_Display #(.active("false")) u_7_segment_display_2 (
    .g(_5_EB_12_out), .f(_5_EB_11_out), .a(_5_EB_6_out), .b(_5_EB_7_out), .e(_5_EB_10_out), .d(_5_EB_9_out),
    .c(_5_EB_8_out), .dp(not_5_out));

  // Notes on the sheet:
  //   S1
  //   S2
endmodule
